# Fritzing sketch Untitled Sketch 3 (saved by Fritzing 0.9.3b)
breadboards: 1

parts:
  Part1 = Arduino Uno (Rev3)
  Part2 = Bluetooth HC-05 Macho
  R1 = Resistor [tolerance=±2% resistance=220 package=THT]
  R2 = Resistor [tolerance=±5% resistance=220 package=THT]
  Mod1 = KY-019 5V Relay Module [package="Breakout board"]
  BULB1 = Incandescent light bulb small [package="bulb sm"]

nets:
  N1: Part1.D10_PWM/SS, Mod1.S
  N2: Part1.D0/RX, Part2.TXD
  N3: Part1.D1/TX, R1.Pin_1
  5V: Part1.5V, Part2.VCC, Mod1.+
  GND: Part1.GND, Part2.GND, R2.Pin_0, Mod1.-
  N4: Mod1.Common, BULB1.1

notes:
  điện
  nguồn

custom parts:
  KY-019 5V Relay Module: KY-019 5V Relay module, used to control AC circuits. (Special thanks to vanepp for fixing the PCB holes and other errors)
